# Fritzing sketch xcontrol1 (saved by Fritzing 0.9.4)

parts:
  R1 = Resistor [tolerance=±5% resistance=27k package=THT]
  R2 = Resistor [tolerance=±5% resistance=82k package=THT]
  R3 = Resistor [tolerance=±5% resistance=200 package=THT]
  R4 = Resistor [tolerance=±5% resistance=240k package=THT]
  R5 = Resistor [tolerance=±1% resistance=82.5k package=THT]
  J2 = female pin header, 1 pin [form="♀ (female)"]
  R6 = Resistor [tolerance=±5% resistance=47k package=THT]
  Pro_Micro1 = SparkFun Pro Micro
  X-Axis = POT [package=alps_pot]
  Y-Axis = POT [package=alps_pot]
  S1 = Pushbutton [package="[THT]"]
  S2 = Pushbutton [package="[THT]"]
  S3 = Pushbutton [package="[THT]"]
  S4 = Pushbutton [package="[THT]"]
  J3 = female pin header, 1 pin [form="♀ (female)"]
  J4 = female pin header, 1 pin [form="♀ (female)"]
  J5 = female pin header, 1 pin [form="♀ (female)"]
  J6 = female pin header, 1 pin [form="♀ (female)"]

nets:
  N1: R1.Pin_0, R2.Pin_0, R3.Pin_1, R4.Pin_1, R5.Pin_0, R6.Pin_1, Pro_Micro1.A3
  N2: R1.Pin_1, J5.pin1
  N3: R2.Pin_1, J6.pin1
  N4: R3.Pin_0, J4.pin1
  N5: R4.Pin_0, J3.pin1
  5V: R5.Pin_1, J2.pin1, Pro_Micro1.VCC, X-Axis.E, Y-Axis.E
  GND: R6.Pin_0, Pro_Micro1.GND, X-Axis.A, Y-Axis.A, S1.Pin_1, S1.Pin_2, S2.Pin_1, S2.Pin_2, S3.Pin_1, S3.Pin_2, S4.Pin_1, S4.Pin_2
  N6: Pro_Micro1.2, S4.Pin_3, S4.Pin_4
  N7: Pro_Micro1.3, S1.Pin_3, S1.Pin_4
  N8: Pro_Micro1.4, S3.Pin_3, S3.Pin_4
  N9: Pro_Micro1.5, S2.Pin_4
  N10: Pro_Micro1.A0, X-Axis.S
  N11: Pro_Micro1.A1, Y-Axis.S

notes:
  Hat connector uses a resistor tree (layout shown as seen from behind)
  5V is always connected to signal line via 82.5kΩ resistor
  Moving hat makes additional parallel connection across other resistors - 27kΩ (R), 200Ω (U), 82kΩ (D), 240kΩ (L).
  So, total resistance at each position:
  Left: 61.1kΩ
  Up: 199.5Ω
  Centre: 82.5kΩ
  Down: 41kΩ
  Right: 20.3kΩ
  A3 reads hat position via potential divider with 47kΩ. Therefore ADC readings are:
  Left: 445
  Up: 1019
  Centre: 370
  Down: 546
  Right: 714
  X-Control 1, 1

custom parts:
  SparkFun Pro Micro: The Pro Micro is similar to the Pro Mini except with an ATmega32U4 on board. The USB transceiver inside the 32U4 allows us to add USB connectivity on-board and do away with bulky external USB interface. Based on: https://github.com/unorthodox-engineers/unorthodox-arduino/blob/master/Unorthodox/fritzing/parts/Pro%20Micro.fzpz
